# Fritzing sketch sketch (saved by Fritzing 0.9.5d)
circuit board: 8.46667cm x 5.64444cm
breadboards: 1

parts:
  U1 = NodeMCU V1.0
  M1 = RioRand LM2596
  M2 = DC Motor [part_number="Water Pump"]
  U2 = L298_BRIDGE_DRIVER [package=powerso20]
  IC4 = Microchip MCP23008 8-bit I/O expander [part_number=MCP23008 package="DIP (Dual Inline) [THT]"]
  valve = DC Motor
  valve1 = DC Motor
  J5 = female pin header, 3 pins [form="♀ (female)"]
  VCC1 = Battery
  4_Channel_Relay1 = 4 Channel Power Relay
  Screw_connector_12v = female pin header, 4 pins [form="♀ (female)"]
  J6 = female pin header, 6 pins [form="♀ (female)"]
  J4 = male pin header, 2 pins [form="♂ (male)"]
  Screw_connector_ground = female pin header, 4 pins [form="♀ (female)"]
  J3 = male pin header, 3 pins [form="♂ (male)"]
  HC-SR04_Sensor_1 = HC-SR04 Ultrasonic Distance Sensor
  Screw_connector_ground1 = female pin header, 3 pins [form="♀ (female)"]

nets (from the pcb view):
  N1: U1.D1, IC4.SCL
  N2: U1.D2, IC4.SDA
  N3: U1.D4, Screw_connector_ground1.pin1
  3V3: U1.3V3, IC4.Reset, IC4.VDD
  GND: U1.GND, M1.Pin_4, IC4.A2, IC4.A1, IC4.A0, IC4.VSS, 4_Channel_Relay1.GND, J3.pin1, J3.pin2, J3.pin3
  N4: U1.D5, U2.ENA, J5.pin1
  N5: U1.D6, Screw_connector_ground1.pin2
  N6: U1.D7, Screw_connector_ground1.pin3
  VCC: U1.Vin, M1.Pin_3, 4_Channel_Relay1.VCC, J4.pin1, J4.pin2, HC-SR04_Sensor_1.VCC
  N7: M1.Pin_1, U2.VS, VCC1.+, 4_Channel_Relay1.COM, Screw_connector_12v.pin1, Screw_connector_12v.pin2, Screw_connector_12v.pin3, Screw_connector_12v.pin4
  N8: M1.Pin_2, U2.GND, valve.pin_2, valve1.pin_2, VCC1.-, Screw_connector_ground.pin1, Screw_connector_ground.pin2, Screw_connector_ground.pin3, Screw_connector_ground.pin4
  N9: M2.pin_1, U2.OUT1
  N10: M2.pin_2, U2.OUT2
  N11: U2.IN1, IC4.GP7, J5.pin2
  N12: U2.IN2, IC4.GP6, J5.pin3
  N13: IC4.GP0, J6.pin6
  N14: IC4.GP1, J6.pin5, HC-SR04_Sensor_1.TRIG
  N15: IC4.GP2, 4_Channel_Relay1.IN1, J6.pin4
  N16: IC4.GP3, 4_Channel_Relay1.IN2, J6.pin3
  N17: IC4.GP4, 4_Channel_Relay1.IN3, J6.pin2
  N18: IC4.GP5, 4_Channel_Relay1.IN4, J6.pin1
  N19: valve.pin_1, 4_Channel_Relay1.NO#21
  N20: valve1.pin_1, 4_Channel_Relay1.NO#18

custom parts:
  NodeMCU V1.0: ESP8266 based NodeMCU
  Microchip MCP23008 8-bit I/O expander: Provides 8-bit, general purpose, parallel I/O expansion for I2C bus. Datasheet: http://ww1.microchip.com/downloads/en/devicedoc/21919e.pdf
  4 Channel Power Relay: A 4 channel power relay. The module operates at 5V.
